# Fritzing sketch 228_14 (saved by Fritzing 0.8.7b)
breadboards: 3

parts:
  U1 = 555 Timer [package="DIP8 [THT]"]
  IC1 = IC, DIP package, 14 pins [chip_label=7400]
  IC3 = IC, DIP package, 14 pins [chip_label=7442]
  IC4 = IC, DIP package, 14 pins [chip_label=74164]
  IC5 = IC, DIP package, 16 pins [chip_label=74283]
  IC6 = IC, DIP package, 16 pins [chip_label="74173 (IP)"]
  IC7 = IC, DIP package, 16 pins [chip_label="74173 (A)"]
  IC8 = IC, DIP package, 16 pins [chip_label="74173 (B)"]
  IC9 = IC, DIP package, 16 pins [chip_label="74173 (LED)"]
  IC10 = IC, DIP package, 16 pins [chip_label="74173 (MAR)"]
  IC11 = IC, DIP package, 16 pins [chip_label="74173 (IR)"]
  IC12 = IC, DIP package, 16 pins [chip_label=74173]
  IC13 = IC, DIP package, 16 pins [chip_label=74173]
  IC14 = IC, DIP package, 16 pins [chip_label=74173]
  IC15 = IC, DIP package, 16 pins [chip_label=74173]
  D1 = LED_BARGRAPH_10 [package=led_bargaph_10]
  IC16 = IC, DIP package, 14 pins [chip_label=7432]
  IC17 = IC, DIP package, 14 pins [chip_label=7404]
  U2 = IC, DIP package, 14 pins [chip_label=7400]
  L1 = Inductor [package="400 mil [THT]"]  # not connected

nets:
  N1: U1.Ground, IC1.pin7, IC4.pin7, D1.H_A, IC17.pin7, U2.pin7
  N2: U1.Trigger, U1.Threshold
  N3: U1.Output, IC1.pin12
  N4: U1.Reset, IC4.pin2
  N5: U1.Vcc_Supply_Voltage, IC1.pin13, IC1.pin14, IC4.pin14, IC17.pin14, U2.pin14
  N6: IC1.pin4, IC4.pin3, D1.A_C, U2.pin13
  N7: IC1.pin5, IC4.pin4, D1.B_C
  N8: IC1.pin6, IC4.pin1
  N9: IC1.pin8, IC4.pin8
  N10: IC1.pin9, IC1.pin10, IC1.pin11
  N11: IC3.pin1, IC12.pin2, IC12.pin10
  N12: IC3.pin2, IC13.pin2, IC13.pin10
  N13: IC3.pin3, IC14.pin2, IC14.pin10
  N14: IC3.pin4, IC15.pin2, IC15.pin10
  N15: IC3.pin7, IC12.pin8, IC13.pin8, IC14.pin8, IC15.pin8
  N16: IC3.pin10, IC3.pin11, IC12.pin15, IC13.pin15, IC14.pin15, IC15.pin15
  N17: IC3.pin14, IC12.pin16, IC13.pin16, IC14.pin16, IC15.pin16
  N18: IC4.pin5, D1.C_C, IC16.pin1, IC16.pin4, IC16.pin10, IC16.pin13, IC17.pin9
  N19: IC5.pin1, IC6.pin13, IC7.pin13, IC8.pin13, IC9.pin13, IC10.pin13, IC11.pin13
  N20: IC5.pin2, IC6.pin4, IC7.pin4, IC8.pin4
  N21: IC5.pin3, IC5.pin7, IC5.pin8, IC6.pin2, IC6.pin8, IC7.pin2, IC7.pin8, IC8.pin2, IC8.pin8, IC9.pin1, IC9.pin2, IC9.pin8, IC10.pin1, IC10.pin2, IC10.pin8, IC11.pin1, IC11.pin2, IC11.pin8
  N22: IC5.pin4, IC6.pin14, IC7.pin14, IC8.pin14, IC9.pin14, IC10.pin14, IC11.pin14
  N23: IC5.pin6, IC6.pin3, IC7.pin3, IC8.pin3
  N24: IC5.pin10, IC6.pin11, IC7.pin11, IC8.pin11, IC9.pin11, IC10.pin11, IC11.pin11
  N25: IC5.pin11, IC6.pin6, IC7.pin6, IC8.pin6
  N26: IC5.pin12, IC5.pin14, IC6.pin10, IC6.pin15, IC7.pin10, IC7.pin15, IC8.pin10, IC8.pin15, IC9.pin10, IC9.pin15, IC10.pin10, IC10.pin15, IC11.pin10, IC11.pin15
  N27: IC5.pin13, IC6.pin12, IC7.pin12, IC8.pin12, IC9.pin12, IC10.pin12, IC11.pin12
  N28: IC5.pin15, IC6.pin5, IC7.pin5, IC8.pin5
  N29: IC5.pin16, IC6.pin16, IC7.pin16, IC8.pin16, IC9.pin16, IC10.pin16, IC11.pin16
  N30: IC6.pin1, IC6.pin9, IC10.pin9
  N31: IC6.pin7, IC7.pin7, IC8.pin7, IC9.pin7, IC10.pin7, IC11.pin7
  N32: IC12.pin1, IC13.pin1, IC14.pin1, IC15.pin1
  N33: IC12.pin3, IC13.pin3, IC14.pin3, IC15.pin3
  N34: IC12.pin4, IC13.pin4, IC14.pin4, IC15.pin4
  N35: IC12.pin5, IC13.pin5, IC14.pin5, IC15.pin5
  N36: IC12.pin6, IC13.pin6, IC14.pin6, IC15.pin6
  N37: IC12.pin7, IC13.pin7, IC14.pin7, IC15.pin7
  N38: IC12.pin9, IC13.pin9, IC14.pin9, IC15.pin9
  N39: IC12.pin11, IC13.pin11, IC14.pin11, IC15.pin11
  N40: IC12.pin12, IC13.pin12, IC14.pin12, IC15.pin12
  N41: IC12.pin13, IC13.pin13, IC14.pin13, IC15.pin13
  N42: IC12.pin14, IC13.pin14, IC14.pin14, IC15.pin14
  N43: IC16.pin2, IC17.pin11
  N44: IC16.pin5, IC17.pin10
  N45: IC16.pin9, IC17.pin12
  N46: IC16.pin12, IC17.pin13
  N47: IC17.pin8, U2.pin9
  N48: U2.pin10, U2.pin11
