# Fritzing sketch lab1 (saved by Fritzing 0.8.3b)
breadboards: 1

parts:
  R1 = Resistor [tolerance=±5% resistance=220 package=THT]
  LED1 = LED - 5mm [color="Red (633nm)" package="5 mm [THT]"]
  IC1 = IC, DIP package, 14 pins [chip_label=7404]
  S1 = Toggle Switch [package=THT]
  R2 = Resistor [tolerance=±5% resistance=220 package=THT]

nets:
  N1: R1.Pin_0, IC1.pin7, S1.L1
  N2: R1.Pin_1, LED1.cathode
  N3: LED1.anode, IC1.pin12
  N4: IC1.pin13, S1.COM, R2.Pin_1
  N5: IC1.pin14, R2.Pin_0
