# Fritzing sketch lab3 (saved by Fritzing 0.8.3b)
breadboards: 1

parts:
  IC1 = IC, DIP package, 14 pins [chip_label=7404]
  IC2 = IC, DIP package, 14 pins [chip_label=7408]
  D1 = LED_BARGRAPH_10 [package=led_bargaph_10]

nets:
  N1: IC1.pin1, IC2.pin6
  N2: IC1.pin2, IC2.pin9, D1.A_A
  N3: IC1.pin7, IC2.pin2, IC2.pin7, IC2.pin12
  N4: IC1.pin10, IC2.pin1
  N5: IC1.pin11, IC2.pin13
  N6: IC1.pin12, IC2.pin5
  N7: IC1.pin13, IC2.pin8
  N8: IC1.pin14, IC2.pin14
  N9: IC2.pin3, IC2.pin4
  N10: IC2.pin10, IC2.pin11
