# Fritzing sketch lab4 (saved by Fritzing 0.8.3b)
breadboards: 1

parts:
  U1 = 555 Timer [package="DIP8 [THT]"]
  C1 = Ceramic Capacitor [capacitance=100nF package="100 mil [THT, multilayer]"]
  IC1 = IC, DIP package, 14 pins [chip_label=7404]
  IC2 = IC, DIP package, 14 pins [chip_label=74164]
  IC3 = IC, DIP package, 14 pins [chip_label=74xx]
  R1 = Resistor [tolerance=±5% resistance=220 package=THT]
  R2 = Resistor [tolerance=±5% resistance=220 package=THT]
  D1 = LED_BARGRAPH_10 [package=led_bargaph_10]
  R3 = Resistor [tolerance=±5% resistance=220 package=THT]
  R4 = Resistor [tolerance=±5% resistance=220 package=THT]
  R5 = Resistor [tolerance=±5% resistance=220 package=THT]
  R6 = Resistor [tolerance=±5% resistance=220 package=THT]

nets:
  N1: U1.Ground, U1.Threshold, C1.0, C1.1, IC1.pin7, IC2.pin7, IC3.pin7, R2.Pin_0
  N2: U1.Output, IC1.pin1
  N3: U1.Discharge, R1.Pin_0, R2.Pin_1
  N4: U1.Vcc_Supply_Voltage, IC1.pin14, IC2.pin9, IC2.pin14, IC3.pin14, R1.Pin_1
  N5: IC1.pin2, IC1.pin3
  N6: IC1.pin4, IC2.pin8
  N7: IC1.pin5, IC3.pin6
  N8: IC1.pin6, IC2.pin1, IC2.pin2
  N9: IC2.pin3, IC3.pin5, D1.D_A
  N10: IC2.pin4, IC3.pin2, D1.C_A
  N11: IC2.pin5, IC3.pin1, D1.B_A
  N12: IC2.pin6, D1.A_A
  N13: IC3.pin3, IC3.pin4
  N14: D1.D_C, R6.Pin_1
  N15: D1.C_C, R5.Pin_1
  N16: D1.B_C, R4.Pin_1
  N17: D1.A_C, R3.Pin_1
  N18: R3.Pin_0, R4.Pin_0, R5.Pin_0, R6.Pin_0
