# Fritzing sketch lab5 (saved by Fritzing 0.8.3b)
breadboards: 1

parts:
  IC1 = IC, DIP package, 16 pins [chip_label=74283]
  IC2 = IC, DIP package, 16 pins [chip_label=_______74173]
  IC3 = IC, DIP package, 16 pins [chip_label=74173]
  IC4 = IC, DIP package, 16 pins [chip_label=74173]
  IC5 = IC, DIP package, 16 pins [chip_label=74175]
  D1 = LED_BARGRAPH_10 [package=led_bargaph_10]

nets:
  N1: IC1.pin1, IC2.pin13, IC3.pin13, IC4.pin13, IC5.pin4
  N2: IC1.pin2, IC1.pin7, IC1.pin8, IC2.pin1, IC2.pin2, IC2.pin8, IC3.pin2, IC3.pin8, IC4.pin2, IC4.pin8, IC5.pin8
  N3: IC1.pin3, IC2.pin4, IC3.pin4, IC4.pin4
  N4: IC1.pin4, IC2.pin14, IC3.pin14, IC4.pin14, IC5.pin5
  N5: IC1.pin5, IC2.pin3, IC3.pin3, IC4.pin3
  N6: IC1.pin6, IC3.pin1, IC4.pin1, IC5.pin1
  N7: IC1.pin10, IC2.pin11, IC3.pin11, IC4.pin11, IC5.pin12
  N8: IC1.pin11, IC1.pin15, IC2.pin9, IC2.pin10, IC2.pin15, IC3.pin10, IC3.pin15, IC4.pin10, IC4.pin15, D1.I_C
  N9: IC1.pin12, IC2.pin6, IC3.pin6, IC4.pin6
  N10: IC1.pin13, IC2.pin12, IC3.pin12, IC4.pin12, IC5.pin13
  N11: IC1.pin14, IC2.pin5, IC3.pin5, IC4.pin5
  N12: IC1.pin16, IC2.pin16, IC3.pin9, IC3.pin16, IC4.pin9, IC4.pin16, IC5.pin16
  N13: IC5.pin2, D1.B_A
  N14: IC5.pin7, D1.A_A
  N15: IC5.pin10, D1.D_A
  N16: IC5.pin15, D1.C_A
