# Fritzing sketch lab6 (saved by Fritzing 0.8.3b)
breadboards: 1

parts:
  IC1 = IC, DIP package, 16 pins [chip_label=7442]
  IC2 = IC, DIP package, 16 pins [chip_label=74173]
  IC3 = IC, DIP package, 16 pins [chip_label=74173]
  IC4 = IC, DIP package, 16 pins [chip_label=74173]
  IC5 = IC, DIP package, 16 pins [chip_label=74173]
  IC6 = IC, DIP package, 16 pins [chip_label=74175]
  IC7 = IC, DIP package, 16 pins [chip_label=_____74175]

nets:
  N1: IC1.pin1, IC2.pin2, IC2.pin10
  N2: IC1.pin2, IC3.pin2, IC3.pin10
  N3: IC1.pin3, IC4.pin2, IC4.pin10
  N4: IC1.pin4, IC5.pin2, IC5.pin10
  N5: IC1.pin5, IC6.pin12
  N6: IC1.pin8, IC2.pin8, IC3.pin8, IC4.pin8, IC5.pin8, IC6.pin8, IC7.pin8
  N7: IC1.pin12, IC1.pin13, IC2.pin15, IC3.pin15, IC4.pin15, IC5.pin15
  N8: IC1.pin14, IC6.pin2
  N9: IC1.pin15, IC6.pin7
  N10: IC1.pin16, IC2.pin16, IC3.pin16, IC4.pin16, IC5.pin16, IC6.pin16, IC7.pin16
  N11: IC2.pin1, IC3.pin1, IC4.pin1, IC5.pin1
  N12: IC2.pin3, IC3.pin3, IC4.pin3, IC5.pin3, IC7.pin5
  N13: IC2.pin4, IC3.pin4, IC4.pin4, IC5.pin4, IC7.pin4
  N14: IC2.pin5, IC3.pin5, IC4.pin5, IC5.pin5, IC7.pin13
  N15: IC2.pin6, IC3.pin6, IC4.pin6, IC5.pin6, IC7.pin12
  N16: IC2.pin7, IC3.pin7, IC4.pin7, IC5.pin7
  N17: IC2.pin9, IC3.pin9, IC4.pin9, IC5.pin9
  N18: IC2.pin11, IC3.pin11, IC4.pin11, IC5.pin11
  N19: IC2.pin12, IC3.pin12, IC4.pin12, IC5.pin12
  N20: IC2.pin13, IC3.pin13, IC4.pin13, IC5.pin13
  N21: IC2.pin14, IC3.pin14, IC4.pin14, IC5.pin14
  N22: IC6.pin1, IC7.pin1
